// Logisim project ProcessadorMipsPIPELINE.circ as structural Verilog: 1 circuit, main circuit main
module main (
  input  in_1,
  input  in_2,
  input  in_3,
  input  in_4,
  input  in_5,
  input  [3:0] in_6,
  input  in_7,
  input  in_8,
  input  in_9,
  output [31:0] out_10,
  output [31:0] out_11,
  output [4:0] out_12,
  output [4:0] out_13,
  output [31:0] out_14,
  output [31:0] out_15
);

  wire CLK;
  wire [4:0] EX_MEM2_q, ID_EX4_q, multiplexer_2_out, rW;
  wire [10:0] ID_EX2_q;
  wire [31:0] adder_1_out, adder_2_out, bit_extender_1_out, EX_MEM0_q, ID_EX3_q, IF_ID_q, mips_alu_1_p5,
       mips_ram_1_p8, mipsprogramrom_1_p2, multiplexer_1_out, multiplexer_4_out, register_1_q,
       registerfile_1_p7, registerfile_1_p8, registerfile_1_p9, shifter_1_out;

  Clock clock_1 (.out(CLK));
  Register #(.width(32)) register_1 (.D(multiplexer_1_out), .en(1'b1), .clk(CLK), .Q(register_1_q), .clr(in_3));
  Adder #(.width(32)) adder_1 (.a(32'h4), .b(register_1_q), .out(adder_1_out));  // open: cin, cout
  Adder #(.width(32)) adder_2 (.a(adder_1_out), .b(shifter_1_out), .out(adder_2_out));  // open: cin, cout
  // MIPSProgramROM mipsprogramrom_1: pin names not known; wires that end beside it: register_1_q, mipsprogramrom_1_p2
  Multiplexer #(.width(32), .enable("false")) multiplexer_1 (
    .in0(adder_1_out), .in1(adder_2_out), .out(multiplexer_1_out), .sel(in_9));
  Register #(.width(32)) IF_ID (
    .D(mipsprogramrom_1_p2), .en(1'b1), .clk(CLK), .Q({IF_ID_q[31:26], out_12, out_13, IF_ID_q[15:0]}));  // open: clr
  assign bit_extender_1_out = {{16{IF_ID_q[15]}}, IF_ID_q[15:0]};  // Bit_Extender bit_extender_1
  Multiplexer #(.width(5), .enable("false")) multiplexer_2 (
    .in0(out_13), .in1(IF_ID_q[15:11]), .out(multiplexer_2_out), .sel(in_1));
  // RegisterFile registerfile_1: pin names not known; wires that end beside it: out_11, CLK, in_2, rW, out_12, out_13, registerfile_1_p7, registerfile_1_p8, registerfile_1_p9
  Register #(.width(32)) ID_EX0 (.D(registerfile_1_p8), .en(1'b1), .clk(CLK), .Q(out_10));  // open: clr
  Register #(.width(32)) ID_EX1 (.D(registerfile_1_p7), .en(1'b1), .clk(CLK), .Q(registerfile_1_p9));  // open: clr
  Register #(.width(11)) ID_EX2 (.D(IF_ID_q[10:0]), .en(1'b1), .clk(CLK), .Q(ID_EX2_q));  // open: clr
  Register #(.width(32)) ID_EX3 (.D(bit_extender_1_out), .en(1'b1), .clk(CLK), .Q(ID_EX3_q));  // open: clr
  Register #(.width(5)) ID_EX4 (.D(multiplexer_2_out), .en(1'b1), .clk(CLK), .Q(ID_EX4_q));  // open: clr
  Multiplexer #(.width(32), .enable("false")) multiplexer_3 (
    .in0(registerfile_1_p9), .in1(ID_EX3_q), .out(out_15), .sel(in_5));
  // Mips_ALU mips_alu_1: pin names not known; wires that end beside it: out_10, out_15, in_6, ID_EX2_q[10:6], mips_alu_1_p5
  Shifter #(.width(32)) shifter_1 (.in(ID_EX3_q), .\dist (5'b00010), .out(shifter_1_out));
  Register #(.width(32)) EX_MEM0 (.D(mips_alu_1_p5), .en(1'b1), .clk(CLK), .Q(EX_MEM0_q));  // open: clr
  Register #(.width(32)) EX_MEM1 (.D(out_15), .en(1'b1), .clk(CLK), .Q(out_14));  // open: clr
  Register #(.width(5)) EX_MEM2 (.D(ID_EX4_q), .en(1'b1), .clk(CLK), .Q(EX_MEM2_q));  // open: clr
  // MIPS_RAM mips_ram_1: pin names not known; wires that end beside it: EX_MEM0_q[19:0], out_14, in_7, 4'b1111, CLK, in_8, in_3, mips_ram_1_p8
  Multiplexer #(.width(32), .enable("false")) multiplexer_4 (
    .in0(mips_ram_1_p8), .in1(EX_MEM0_q), .out(multiplexer_4_out), .sel(in_4));
  Register #(.width(32)) MEM_WB0 (.D(multiplexer_4_out), .en(1'b1), .clk(CLK), .Q(out_11));  // open: clr
  Register #(.width(5)) MEM_WB1 (.D(EX_MEM2_q), .en(1'b1), .clk(CLK), .Q(rW));  // open: clr

  // Other names for the same wires on the sheet: ALUOp[3:0] = in_6; ALUSrc = in_5; Branch = in_9; MemRead = in_8;
  //   MemtoReg = in_4; MemWhite = in_7; REGDest = in_1; REGWrite = in_2; RST = in_3

  // Notes on the sheet:
  //   contents of mipsprogramrom_1 (hex, n*v repeats v):
  //   addiu $3,$3,2 Subu $1,$3,$2 addiu $2,$2,4 Subu $1,$1,$2
endmodule
